// Logisim project exp08-priority-encoder.circ as structural Verilog: 1 circuit, main circuit main
module main (
  input  EN,
  input  I0,
  input  I1,
  input  I2,
  input  I3,
  output V,
  output Y0,
  output Y1
);

  wire G1_out, G2_out, G3_out, G4_out, G5_out, undriven, undriven_2, undriven_3, undriven_4, undriven_5,
       undriven_6, undriven_7;

  not G1 (G1_out, undriven_4);
  or G4 (G4_out, undriven_6, undriven_5);
  or G5 (G5_out, undriven_7, I2, undriven_3, I0);
  and G2 (G2_out, I1, G1_out);
  and G6 (Y1, G4_out, undriven);
  and G8 (V, G5_out, undriven_2);
  or G3 (G3_out, I3, G2_out);
  and G7 (Y0, G3_out, EN);
endmodule
