// Logisim project adder_subtractor.circ as structural Verilog: 1 circuit, main circuit main
// Mode
module main (
  input  A3,
  input  S3,
  input  B3,
  input  Cout,
  input  A2,
  input  Mode,
  input  S2,
  input  B2,
  input  A1,
  input  S1,
  input  B1,
  input  A0,
  input  S0,
  input  B0
);

  wire adder_2_cout, adder_3_cout, adder_4_cout, xor_1_out, xor_2_out, xor_3_out, xor_4_out;

  xor xor_1 (xor_1_out, Mode, B1);
  xor xor_2 (xor_2_out, Mode, B0);
  xor xor_3 (xor_3_out, Mode, B3);
  xor xor_4 (xor_4_out, Mode, B2);
  Adder #(.width(1)) adder_1 (.a(A3), .b(xor_3_out), .out(S3), .cin(adder_2_cout), .cout(Cout));
  Adder #(.width(1)) adder_2 (.a(A2), .b(xor_4_out), .out(S2), .cin(adder_3_cout), .cout(adder_2_cout));
  Adder #(.width(1)) adder_3 (.a(A1), .b(xor_1_out), .out(S1), .cin(adder_4_cout), .cout(adder_3_cout));
  Adder #(.width(1)) adder_4 (.a(A0), .b(xor_2_out), .out(S0), .cin(Mode), .cout(adder_4_cout));
endmodule
