// Logisim project exp8_gates.circ as structural Verilog: 1 circuit, main circuit main
module main (
  input  E_IN,
  input  D3,
  input  D2,
  input  D1,
  input  D0,
  output V,
  output OUT_1,
  output OUT_2
);

  wire and_3_out, not_1_out, or_1_out, or_2_out, or_3_out;

  or or_1 (or_1_out, D3, D2, D1, D0);
  not not_1 (not_1_out, D2);
  and and_1 (V, E_IN, or_1_out);
  or or_2 (or_2_out, D3, D2);
  and and_2 (OUT_1, or_2_out, E_IN);
  and and_3 (and_3_out, not_1_out, D1);
  or or_3 (or_3_out, and_3_out, D3);
  and and_4 (OUT_2, or_3_out, E_IN);
endmodule
