// Logisim project priority_plexers.circ as structural Verilog: 1 circuit, main circuit main
module main (
  input  w0,
  input  w1,
  input  w2,
  input  w3,
  input  E,
  output y1,
  output y2,
  output z
);

  Priority_Encoder #(.select(2)) priority_encoder_1 (
    .in0(w0), .in1(w1), .in2(w2), .in3(w3), .out({y2, y1}), .gs(z), .en_in(E));  // open: en_out
endmodule
